// Logisim project Circuit.circ as structural Verilog: 3 circuits, main circuit main
module main (
);

  wire clock_1_out, cpu_main_ram_load, d_ff_1_qn, or_1_out, ram_slot_1_ram_clock_out,
       ram_slot_1_ram_load_out, ram_slot_1_ram_store_out, Reset_out;
  wire [15:0] cpu_main_ram_addr, main_ram_dout, ram_slot_1_ram_addr_out, ram_slot_1_ram_data_out,
       ram_slot_1_ram_value_out;

  Clock clock_1 (.out(clock_1_out));
  Button Reset (.out(Reset_out));
  ram_slot ram_slot_1 (
    .RAM_LOAD_IN(cpu_main_ram_load), .RAM_CLOCK_IN(clock_1_out), .RAM_ADDR_IN(cpu_main_ram_addr),
    .RAM_DATA_IN(main_ram_dout), .RAM_ADDR_OUT(ram_slot_1_ram_addr_out),
    .RAM_VALUE_OUT(ram_slot_1_ram_value_out), .RAM_DATA_OUT(ram_slot_1_ram_data_out),
    .RAM_LOAD_OUT(ram_slot_1_ram_load_out), .RAM_STORE_OUT(ram_slot_1_ram_store_out),
    .RAM_CLOCK_OUT(ram_slot_1_ram_clock_out));  // open: RAM_STORE_IN, RAM_VALUE_IN
  RAM #(.addrWidth(16), .dataWidth(16), .\type ("nonvolatile")) main_ram (
    .addr(ram_slot_1_ram_addr_out), .we(ram_slot_1_ram_store_out), .oe(ram_slot_1_ram_load_out),
    .clk(ram_slot_1_ram_clock_out), .din(ram_slot_1_ram_value_out), .dout(main_ram_dout));
  D_Flip_Flop d_ff_1 (.D(1'b1), .clk(clock_1_out), .Qn(d_ff_1_qn));  // open: Q, preset, reset
  or or_1 (or_1_out, Reset_out, d_ff_1_qn);
  cpu cpu_main (
    .CLOCK(clock_1_out), .RAM_OUT(ram_slot_1_ram_data_out), .RESET(or_1_out), .RAM_ADDR(cpu_main_ram_addr),
    .RAM_LOAD(cpu_main_ram_load));
endmodule

module cpu (
  input  RESET,
  input  CLOCK,
  input  [15:0] RAM_OUT,
  output [15:0] RAM_ADDR,
  output RAM_LOAD
);

  wire adder_1_cout, alu_enable, alu_flag_carry, alu_flag_zero, and_1_out, and_2_out, comparator_1_eq,
       comparator_1_lt, decoder_1_out1, decoder_1_out2, decoder_1_out3, decoder_2_out0, decoder_2_out1,
       decoder_2_out2, demultiplexer_1_out0, demultiplexer_1_out1, demultiplexer_1_out2,
       demultiplexer_1_out3, demultiplexer_1_out4, demultiplexer_1_out5, demultiplexer_1_out6,
       demultiplexer_1_out7, demultiplexer_2_out0, demultiplexer_2_out1, demultiplexer_2_out2,
       demultiplexer_2_out3, demultiplexer_2_out4, demultiplexer_2_out5, demultiplexer_2_out6,
       demultiplexer_2_out7, demultiplexer_2_out8, demultiplexer_2_out9, demultiplexer_2_out10,
       demultiplexer_2_out11, demultiplexer_2_out12, demultiplexer_2_out13, demultiplexer_2_out14,
       demultiplexer_2_out15, jump, multiplexer_1_out, multiplexer_3_out, or_3_out, or_4_out, or_5_out,
       or_6_out, or_7_out, or_8_out, or_9_out, or_10_out, or_11_out, or_12_out, or_13_out, or_14_out,
       or_15_out, or_16_out, or_17_out, or_18_out, or_19_out, pla_1_out, r8_write, r16_write, RESET_t,
       STAGE_EXE1, STAGE_EXE2, STAGE_LOAD, subtractor_1_bout, xor_1_out;
  wire [2:0] alu_operation;
  wire [7:0] mux8x_value, mux8y_value, or_1_out, or_2_out, r8_wr_value;
  wire [15:0] adder_1_out, alu_result, alu_value_a, alu_value_b, cur_instr, demultiplexer_3_out0,
       demultiplexer_3_out1, demultiplexer_3_out2, demultiplexer_4_out0, demultiplexer_4_out1,
       demultiplexer_4_out2, jump_target, mux16x_value, mux16y_value, pc, r16_wr_value, ray_q, rby_q, rcy_q,
       rdy_q, rey_q, rfy_q, rgy_q, rhy_q, subtractor_1_out;

  Pull_Resistor pull_resistor_1 (.node(r8_wr_value));
  Pull_Resistor pull_resistor_2 (.node(r16_wr_value));
  Pull_Resistor pull_resistor_3 (.node(r16_write));
  Demultiplexer #(.select(3)) demultiplexer_1 (
    .out0(demultiplexer_1_out0), .out1(demultiplexer_1_out1), .out2(demultiplexer_1_out2),
    .out3(demultiplexer_1_out3), .out4(demultiplexer_1_out4), .out5(demultiplexer_1_out5),
    .out6(demultiplexer_1_out6), .out7(demultiplexer_1_out7), .in(r16_write), .sel(cur_instr[2:0]));
  Pull_Resistor pull_resistor_4 (.node(r8_write));
  Demultiplexer #(.select(4)) demultiplexer_2 (
    .out0(demultiplexer_2_out0), .out1(demultiplexer_2_out1), .out2(demultiplexer_2_out2),
    .out3(demultiplexer_2_out3), .out4(demultiplexer_2_out4), .out5(demultiplexer_2_out5),
    .out6(demultiplexer_2_out6), .out7(demultiplexer_2_out7), .out8(demultiplexer_2_out8),
    .out9(demultiplexer_2_out9), .out10(demultiplexer_2_out10), .out11(demultiplexer_2_out11),
    .out12(demultiplexer_2_out12), .out13(demultiplexer_2_out13), .out14(demultiplexer_2_out14),
    .out15(demultiplexer_2_out15), .in(r8_write), .sel(cur_instr[3:0]));
  Counter #(.max('hffff), .width(16)) ProgramCounter (
    .clr(RESET), .load(jump), .count(STAGE_LOAD), .clk(CLOCK), .D(jump_target), .Q(pc));  // open: up, carry
  D_Flip_Flop #(.trigger("falling")) d_ff_1 (
    .D(STAGE_EXE2), .clk(CLOCK), .Q(STAGE_LOAD), .preset(RESET));  // open: Qn, reset
  assign or_1_out = r8_wr_value | r16_wr_value[7:0];  // OR_Gate or_1, 8 bits wide
  assign or_2_out = r8_wr_value | r16_wr_value[15:8];  // OR_Gate or_2, 8 bits wide
  D_Flip_Flop #(.trigger("falling")) d_ff_2 (
    .D(STAGE_LOAD), .clk(CLOCK), .Q(STAGE_EXE1), .reset(RESET));  // open: Qn, preset
  D_Flip_Flop #(.trigger("falling")) d_ff_3 (
    .D(STAGE_EXE1), .clk(CLOCK), .Q(STAGE_EXE2), .reset(RESET));  // open: Qn, preset
  assign RAM_ADDR = STAGE_LOAD ? pc : 16'bz;  // Controlled_Buffer controlled_buffer_1
  Pull_Resistor pull_resistor_5 (.node(alu_value_a));
  Demultiplexer #(.enable("true"), .select(3), .width(16)) demultiplexer_3 (
    .out0(demultiplexer_3_out0), .out1(demultiplexer_3_out1), .out2(demultiplexer_3_out2), .in(alu_value_a),
    .sel(alu_operation), .en(alu_enable));  // open: out3, out4, out5, out6, out7
  Pull_Resistor pull_resistor_6 (.node(alu_value_b));
  Demultiplexer #(.enable("true"), .select(3), .width(16)) demultiplexer_4 (
    .out0(demultiplexer_4_out0), .out1(demultiplexer_4_out1), .out2(demultiplexer_4_out2), .in(alu_value_b),
    .sel(alu_operation), .en(alu_enable));  // open: out3, out4, out5, out6, out7
  Pull_Resistor pull_resistor_7 (.node(alu_operation));
  assign RAM_LOAD = STAGE_LOAD ? STAGE_LOAD : 1'bz;  // Controlled_Buffer controlled_buffer_2
  or or_3 (or_3_out, demultiplexer_1_out0, demultiplexer_2_out0);
  or or_4 (or_4_out, demultiplexer_1_out0, demultiplexer_2_out1);
  or or_5 (or_5_out, demultiplexer_1_out1, demultiplexer_2_out2);
  or or_6 (or_6_out, demultiplexer_1_out1, demultiplexer_2_out3);
  or or_7 (or_7_out, demultiplexer_1_out2, demultiplexer_2_out4);
  or or_8 (or_8_out, demultiplexer_1_out2, demultiplexer_2_out5);
  or or_9 (or_9_out, demultiplexer_1_out3, demultiplexer_2_out6);
  or or_10 (or_10_out, demultiplexer_1_out3, demultiplexer_2_out7);
  or or_11 (or_11_out, demultiplexer_1_out4, demultiplexer_2_out8);
  or or_12 (or_12_out, demultiplexer_1_out4, demultiplexer_2_out9);
  or or_13 (or_13_out, demultiplexer_1_out5, demultiplexer_2_out10);
  or or_14 (or_14_out, demultiplexer_1_out5, demultiplexer_2_out11);
  or or_15 (or_15_out, demultiplexer_1_out6, demultiplexer_2_out12);
  or or_16 (or_16_out, demultiplexer_1_out6, demultiplexer_2_out13);
  or or_17 (or_17_out, demultiplexer_1_out7, demultiplexer_2_out14);
  or or_18 (or_18_out, demultiplexer_1_out7, demultiplexer_2_out15);
  Adder #(.width(16)) adder_1 (
    .a(demultiplexer_3_out0), .b(demultiplexer_4_out0), .out(adder_1_out), .cout(adder_1_cout));  // open: cin
  Subtractor #(.width(16)) subtractor_1 (
    .a(demultiplexer_3_out1), .b(demultiplexer_4_out1), .out(subtractor_1_out), .bout(subtractor_1_bout));  // open: bin
  Comparator #(.mode("unsigned"), .width(16)) comparator_1 (
    .a(demultiplexer_3_out2), .b(demultiplexer_4_out2), .eq(comparator_1_eq), .lt(comparator_1_lt));  // open: gt
  Register #(.width(16)) CurInstr (.D(RAM_OUT), .en(STAGE_LOAD), .clk(CLOCK), .Q(cur_instr), .clr(RESET_t));
  Register rax (.D(or_2_out), .en(or_3_out), .clk(CLOCK), .Q(ray_q[15:8]), .clr(RESET));
  Register ray (.D(or_1_out), .en(or_4_out), .clk(CLOCK), .Q(ray_q[7:0]));  // open: clr
  Register rbx (.D(or_2_out), .en(or_5_out), .clk(CLOCK), .Q(rby_q[15:8]), .clr(RESET));
  Register rby (.D(or_1_out), .en(or_6_out), .clk(CLOCK), .Q(rby_q[7:0]), .clr(RESET));
  Register rcx (.D(or_2_out), .en(or_7_out), .clk(CLOCK), .Q(rcy_q[15:8]), .clr(RESET));
  Register rcy (.D(or_1_out), .en(or_8_out), .clk(CLOCK), .Q(rcy_q[7:0]), .clr(RESET));
  Register rdx (.D(or_2_out), .en(or_9_out), .clk(CLOCK), .Q(rdy_q[15:8]), .clr(RESET));
  Register rdy (.D(or_1_out), .en(or_10_out), .clk(CLOCK), .Q(rdy_q[7:0]), .clr(RESET));
  Register rex (.D(or_2_out), .en(or_11_out), .clk(CLOCK), .Q(rey_q[15:8]));  // open: clr
  Register rey (.D(or_1_out), .en(or_12_out), .clk(CLOCK), .Q(rey_q[7:0]), .clr(RESET));
  Register rfx (.D(or_2_out), .en(or_13_out), .clk(CLOCK), .Q(rfy_q[15:8]), .clr(RESET));
  Register rfy (.D(or_1_out), .en(or_14_out), .clk(CLOCK), .Q(rfy_q[7:0]), .clr(RESET));
  Register rgx (.D(or_2_out), .en(or_15_out), .clk(CLOCK), .Q(rgy_q[15:8]), .clr(RESET));
  Register rgy (.D(or_1_out), .en(or_16_out), .clk(CLOCK), .Q(rgy_q[7:0]), .clr(RESET));
  Register rhx (.D(or_2_out), .en(or_17_out), .clk(CLOCK), .Q(rhy_q[15:8]), .clr(RESET));
  Register rhy (.D(or_1_out), .en(or_18_out), .clk(CLOCK), .Q(rhy_q[7:0]), .clr(RESET));
  Multiplexer #(.select(3)) multiplexer_1 (
    .in0(adder_1_cout), .in1(subtractor_1_bout), .in2(comparator_1_lt), .out(multiplexer_1_out),
    .sel(alu_operation));  // open: in3, in4, in5, in6, in7
  Multiplexer #(.select(3), .width(16)) multiplexer_2 (
    .in0(adder_1_out), .in1(subtractor_1_out), .in2(demultiplexer_3_out2), .out(alu_result),
    .sel(alu_operation));  // open: in3, in4, in5, in6, in7
  Register #(.width(1)) alu_f_carry (
    .D(multiplexer_1_out), .en(alu_enable), .clk(CLOCK), .Q(alu_flag_carry), .clr(RESET));
  PLA #(.in_width(16), .out_width(1), .\table ("0000000000000000 1")) pla_1 (.in(alu_result), .out(pla_1_out));
  Register #(.width(1)) alu_f_zero (
    .D(multiplexer_3_out), .en(alu_enable), .clk(CLOCK), .Q(alu_flag_zero), .clr(RESET));
  Multiplexer #(.select(3)) multiplexer_3 (
    .in0(pla_1_out), .in1(pla_1_out), .in2(comparator_1_eq), .out(multiplexer_3_out), .sel(alu_operation));  // open: in3, in4, in5, in6, in7
  Multiplexer #(.select(3), .width(16)) multiplexer_4 (
    .in0(ray_q), .in1(rby_q), .in2(rcy_q), .in3(rdy_q), .in4(rey_q), .in5(rfy_q), .in6(rgy_q), .in7(rhy_q),
    .out(mux16x_value), .sel(cur_instr[8:6]));
  Multiplexer #(.select(3), .width(16)) multiplexer_5 (
    .in0(ray_q), .in1(rby_q), .in2(rcy_q), .in3(rdy_q), .in4(rey_q), .in5(rfy_q), .in6(rgy_q), .in7(rhy_q),
    .out(mux16y_value), .sel(cur_instr[5:3]));
  Multiplexer #(.select(4), .width(8)) multiplexer_6 (
    .in0(ray_q[15:8]), .in1(ray_q[7:0]), .in2(rby_q[15:8]), .in3(rby_q[7:0]), .in4(rcy_q[15:8]),
    .in5(rcy_q[7:0]), .in6(rdy_q[15:8]), .in7(rdy_q[7:0]), .in8(rey_q[15:8]), .in9(rey_q[7:0]),
    .in10(rfy_q[15:8]), .in11(rfy_q[7:0]), .in12(rgy_q[15:8]), .in13(rgy_q[7:0]), .in14(rhy_q[15:8]),
    .in15(rhy_q[7:0]), .out(mux8x_value), .sel(cur_instr[11:8]));
  Multiplexer #(.select(4), .width(8)) multiplexer_7 (
    .in0(ray_q[15:8]), .in1(ray_q[7:0]), .in2(rby_q[15:8]), .in3(rby_q[7:0]), .in4(rcy_q[15:8]),
    .in5(rcy_q[7:0]), .in6(rdy_q[15:8]), .in7(rdy_q[7:0]), .in8(rey_q[15:8]), .in9(rey_q[7:0]),
    .in10(rfy_q[15:8]), .in11(rfy_q[7:0]), .in12(rgy_q[15:8]), .in13(rgy_q[7:0]), .in14(rhy_q[15:8]),
    .in15(rhy_q[7:0]), .out(mux8y_value), .sel(cur_instr[7:4]));
  Decoder #(.select(4)) decoder_1 (
    .out1(decoder_1_out1), .out2(decoder_1_out2), .out3(decoder_1_out3), .sel(cur_instr[15:12]),
    .en(STAGE_EXE1));  // open: out0, out4, out5, out6, out7, out8, out9, out10, out11, out12, out13, out14, out15
  assign r8_write = decoder_1_out1 ? 1'b1 : 1'bz;  // Controlled_Buffer controlled_buffer_3
  assign r8_wr_value = decoder_1_out1 ? cur_instr[11:4] : 8'bz;  // Controlled_Buffer controlled_buffer_4
  Decoder #(.select(2)) decoder_2 (
    .out0(decoder_2_out0), .out1(decoder_2_out1), .out2(decoder_2_out2), .sel(cur_instr[10:9]),
    .en(decoder_1_out3));  // open: out3
  assign alu_value_a = decoder_1_out2 ? mux16x_value : 16'bz;  // Controlled_Buffer controlled_buffer_5
  assign alu_value_b = decoder_1_out2 ? mux16y_value : 16'bz;  // Controlled_Buffer controlled_buffer_6
  assign alu_enable = decoder_1_out2 ? 1'b1 : 1'bz;  // Controlled_Buffer controlled_buffer_7
  assign r16_write = decoder_1_out2 ? 1'b1 : 1'bz;  // Controlled_Buffer controlled_buffer_8
  assign r16_wr_value = decoder_1_out2 ? alu_result : 16'bz;  // Controlled_Buffer controlled_buffer_9
  assign alu_operation = decoder_1_out2 ? cur_instr[11:9] : 3'bz;  // Controlled_Buffer controlled_buffer_10
  and and_1 (and_1_out, decoder_2_out2, alu_flag_zero);
  and and_2 (and_2_out, decoder_2_out1, alu_flag_carry);
  or or_19 (or_19_out, and_1_out, and_2_out, decoder_2_out0);
  xor xor_1 (xor_1_out, or_19_out, cur_instr[11]);
  assign jump_target = xor_1_out ? mux16x_value : 16'bz;  // Controlled_Buffer controlled_buffer_11
  assign jump = xor_1_out ? 1'b1 : 1'bz;  // Controlled_Buffer controlled_buffer_12

  // Other names for the same wires on the sheet: mux8w[3:0] = cur_instr[3:0]; mux16w[2:0] = cur_instr[2:0];
  //   mux16y[2:0] = cur_instr[5:3]; mux8y[3:0] = cur_instr[7:4]; op_value8[7:0] = cur_instr[11:4];
  //   mux16x[2:0] = cur_instr[8:6]; mux8x[3:0] = cur_instr[11:8]; op16_sub[2:0] = cur_instr[11:9];
  //   opcode[3:0] = cur_instr[15:12]

  // Notes on the sheet:
  //   INPUTS
  //   pipeline thing
  //   Program Counter
  //   Registers, r1-16
  //   8 bit but can be combined
  //   A L U
  //   alu_enable?
  //   not sure if using pla to compare a number to zero is a good idea...
  //   loads V8 into rW8
  //   load u8
  //   alu16
  //   INSTRUCTIONS
  //   performs an alu operation 
  //   specified in op16sub
  //   on rX16 and rY16 and
  //    stores the result in rW16
  //   jump16
  //   jumps to rX16
  //   0x0 - always
  //   0x1 - if zero
  //   0x2 - if carry
  //   0x3 - never/noop
  //   bits 0-2 of op16sub specify the condition
  //   bit 3 inverts the condition
endmodule

module ram_slot (
  input  [15:0] RAM_ADDR_IN,
  input  [15:0] RAM_VALUE_IN,
  input  [15:0] RAM_DATA_IN,
  input  RAM_LOAD_IN,
  input  RAM_STORE_IN,
  input  RAM_CLOCK_IN,
  output [15:0] RAM_ADDR_OUT,
  output [15:0] RAM_VALUE_OUT,
  output [15:0] RAM_DATA_OUT,
  output RAM_LOAD_OUT,
  output RAM_STORE_OUT,
  output RAM_CLOCK_OUT
);


  assign RAM_ADDR_OUT = RAM_ADDR_IN;
  assign RAM_CLOCK_OUT = RAM_CLOCK_IN;
  assign RAM_DATA_OUT = RAM_DATA_IN;
  assign RAM_LOAD_OUT = RAM_LOAD_IN;
  assign RAM_STORE_OUT = RAM_STORE_IN;
  assign RAM_VALUE_OUT = RAM_VALUE_IN;
endmodule
